# Fritzing sketch DHT_LCD (saved by Fritzing 0.9.2b)
circuit board: 8.46667cm x 5.64444cm
breadboards: 2

parts:
  Part1 = Arduino Nano (Rev3.0)
  U2 = LCD-16X2 [package=lcd-16x2]
  DHT1 = DHT11 Humitidy and Temperature Sensor (3 pins)
  R1 = Rotary Potentiometer (Small) [maximum_resistance=100kΩ package=THT]
  R2 = Resistor [tolerance=±5% resistance=220 package=THT]

nets:
  GND: Part1.GND, U2.VSS, U2.R_W, U2.K, DHT1.GND, R1.leg1
  N1: Part1.D4, U2.RS
  N2: Part1.D5, U2.E
  N3: Part1.D6, U2.DB4
  N4: Part1.D7, DHT1.DATA
  N5: Part1.D8, U2.DB5
  N6: Part1.D9, U2.DB6
  N7: Part1.D10, U2.DB7
  5V: Part1.5V, U2.A, DHT1.VDD, R1.leg2, R2.Pin_0
  N8: U2.VDD, R2.Pin_1
  N9: U2.VO, R1.wiper

custom parts:
  DHT11 Humitidy and Temperature Sensor (3 pins): DHT11 Humidity and Temperature Sensor (3 pins) from the design created by John De Cristofaro for Adafruit Industries.

// code stored in the sketch: DHT_LCD.ino


  /*----------( Declare DHT11 )----------*/
  //the following is setup for sensor
#include "dht.h"
dht DHT;

  //connected digital 7 to DHT11 pin2

#define DHT_PIN 7

  //define what sensor you're using
  /*
  DHT11-Pin Define & connected
  Pin1 to VCC
  Pin2 to what pin we define, this project is Digital 2 (line 3)
  Pin3 means nothing
  Pin4 to GND
  */

  /*----------( Declare LCD )----------*/
#include <Wire.h>
#include <LiquidCrystal.h>

// Define lcd pins as header labels

const int rs = 4, en = 5, d4 = 6, d5 = 8, d6 = 9, d7 = 10;

LiquidCrystal lcd(rs, en, d4, d5, d6, d7);

  /*----------( Declare Auduino Setup & Loop )----------*/
void setup()
{
	// Initialize 16x2 LCD
  lcd.begin(16, 2);
}

void loop()
{
	
	//Read DHT sensor

  int chk = DHT.read11(DHT_PIN);
  
	//Move cursor to begin line 0, write static content
  lcd.setCursor(0, 0);
  lcd.print("Temp: ");
	
	//Advance cursor, write DHT temperature and unit
  lcd.setCursor(6, 0);
  lcd.print(DHT.temperature);
  lcd.print(" C");
	
	//Move cursor to begin line 1, write static content
  lcd.setCursor(0, 1);
  lcd.print("RH:");

	//Advance cursor, write DHT humidity and "unit"
  lcd.setCursor(6, 1);
  lcd.print(DHT.humidity);
  lcd.print("%");
	
	//Wait 2 seconds
		//DHT11 has max sample rate of 1 Hz
		//DHT22 has max sample rate of 2 Hz
  delay(2000);
  
}
